# Fritzing sketch circuit (saved by Fritzing 0.9.3b)
stripboards: 1

parts:
  IC1 = IC, DIP package, 20 pins [chip_label=ATtiny261A]
  S1 = Pushbutton [package="[THT]"]
  S2 = Pushbutton [package="[THT]"]
  S3 = Pushbutton [package="[THT]"]
  S4 = Pushbutton [package="[THT]"]
  S5 = Pushbutton [package="[THT]"]
  LED2 = LED - 3mm [color="Red (633nm)" package="3 mm [THT]"]
  LED3 = LED - 3mm [color="Green (555nm)" package="3 mm [THT]"]
  C1 = Ceramic Capacitor [capacitance=100nF package="100 mil [THT, multilayer]"]
  J1 = male pin header, 6 pins [form="♂ (male)"]
  LED4 = LED - 3mm [color="Red (633nm)" package="3 mm [THT]"]
  R4 = Resistor [tolerance=±5% resistance=220 package=THT]
  TRS2 = Audio Jack (TRS) 3.5mm [package="4Ucon 08780 [THT]"]
  TRS3 = Audio Jack (TRS) 3.5mm [package="4Ucon 08780 [THT]"]

nets:
  N1: IC1.pin1, J1.pin4
  N2: IC1.pin2, J1.pin5
  N3: IC1.pin3, J1.pin6
  N4: IC1.pin4, TRS3.Ring
  N5: IC1.pin5, IC1.pin7, IC1.pin12, C1.0, J1.pin2, TRS2.Ring, TRS3.Tip
  N6: IC1.pin6, S1.Pin_3, S1.Pin_4, S2.Pin_1, S2.Pin_2, S3.Pin_3, S3.Pin_4, S4.Pin_1, S4.Pin_2, S5.Pin_1, S5.Pin_2, C1.1, J1.pin1, R4.Pin_0, TRS2.Sleeve, TRS3.Sleeve
  N7: IC1.pin8, S4.Pin_3, S4.Pin_4
  N8: IC1.pin9, S1.Pin_1, S1.Pin_2
  N9: IC1.pin10, J1.pin3
  N10: IC1.pin11, TRS2.Tip
  N11: IC1.pin13, S2.Pin_3, S2.Pin_4
  N12: IC1.pin14, LED3.anode
  N13: IC1.pin17, LED2.cathode
  N14: IC1.pin18, LED4.cathode
  N15: IC1.pin19, S3.Pin_1, S3.Pin_2
  N16: IC1.pin20, S5.Pin_3, S5.Pin_4
  N17: LED2.anode, LED3.cathode, LED4.anode, R4.Pin_1
